# Fritzing sketch SmartWatchFritzing (saved by Fritzing 0.9.4)
circuit board: 6.4cm x 3cm
breadboards: 1

parts:
  J2 = double row female pin header, 6 pins [form="♀ (female)"]
  Part4 = TMP006 Thermopile Sensor
  Part6 = Adafruit ADS1015 12Bit I2C ADC [part_number="Adafruit #1083"]
  Part7 = Adafruit ADXL345 [part_number="Adafruit #1231"]

nets (from the schematic view):
  VCC: J2.pin1, Part4.VCC, Part6.VDD, Part7.3.3V
  N1: J2.pin2, Part4.SDA, Part6.SDA, Part7.SDA/SDIO
  N2: J2.pin3, Part4.SCL, Part6.SCL, Part7.SCL
  GND: J2.pin6, Part4.GND, Part6.GND, Part7.GND

notes:
  3V3
  SDA
  SCL
  5V
  GND

custom parts:
  TMP006 Thermopile Sensor: Unlike all the other temperature sensors we have, this breakout has a really cool IR sensor from TI that can measure the temperature of an object without touching it! Simply point the sensor towards what you want to measure and it will detect the temperature by absorbing IR waves emitted. The embedded thermopile sensor generates a very very small voltage depending on how much IR there is, and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
  Adafruit ADS1015 12Bit I2C ADC: For microcontrollers without an analog-to-digital converter or when you want a higher-precision ADC, the ADS1015 provides 12-bit precision at 3300 samples/second over I2C. The chip can be configured as 4 single-ended input channels, or two differential channels. As a nice bonus, it even includes a programmable gain amplifier, up to x16, to help boost up smaller single/differential signals to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
  Adafruit ADXL345: Filling out our accelerometer offerings, we now have the really lovely digital ADXL345 from Analog Devices, a triple-axis accelerometer with digital I2C and SPI interface breakout. We added an on-board 3.3V regulator and logic-level shifting circuitry, making it a perfect choice for interfacing with any 3V or 5V microcontroller such as the Arduino. The sensor has three axes of measurements, X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
